# Fritzing sketch SAC schematics (saved by Fritzing 0.9.3b)
breadboards: 1

parts:
  Part2 = Arduino Uno (Rev3) - ICSP
  Part3 = Real Time Clock Module - DS1307 RTC Breakout Board
  M1 = Humidity and Temperature Sensor DHT11
  Part4 = LCD1602-I2C
  BT1 = Bluetooth HC-06u [package=THT]

nets:
  N1: Part2.A4/SDA, Part3.SDA, Part4.SDA
  N2: Part2.A5/SCL, Part3.SCL, Part4.SCL
  N3: Part2.D2, BT1.TXD
  N4: Part2.D3_PWM, BT1.RXD
  N5: Part2.D7, M1.Data
  VCC: Part2.5V, Part3.5V, M1.Vcc, Part4.VCC, BT1.VCC
  GND: Part2.GND, Part3.GND, M1.GND, Part4.GND, BT1.GND

custom parts:
  Humidity and Temperature Sensor DHT11: Digital relative humidity & temperature sensor DHT11
  LCD1602-I2C: A standard character display, usually with 2x16 characters. Comes in many colors with LCM1602 IIC attached.
  Bluetooth HC-06u: Bluetooth HC-06 - face up, pins down 16.5mm x 37.5mm PCB
